# Fritzing sketch crowler (saved by Fritzing 1.0.6)
breadboards: 1

parts:
  Компонент1 = Arduino Uno (Rev3)
  Mod1 = ESP32 - CAM
  HC-SR04_Sensor_1 = HC-SR04 Ultrasonic Distance Sensor
  HC-SR04_Sensor_2 = HC-SR04 Ultrasonic Distance Sensor
  HC-SR04_Sensor_3 = HC-SR04 Ultrasonic Distance Sensor
  MPU6050 = InvenSense MPU6050
  J1 = XL4015 DC-DC CC CV module (blue)
  J2 = Basic Servo
  J3 = Piezo Speaker
  Компонент2 = TXB0108 8-channel Bi-directional Logic Level Converter
  S1 = Square Pushbutton
  C1 = Electrolytic Capacitor [capacitance=1000μF voltage=35V package="1010 [SMD, electrolytic]"]
  C3 = Electrolytic Capacitor [capacitance=1000μF voltage=35V package="1010 [SMD, electrolytic]"]
  M1 = DC Motor [voltage_(max)=6V voltage_(min)=3V]
  M2 = DC Motor [voltage_(max)=6V voltage_(min)=3V]
  TB6612FNG = Motor Driver 1A Dual TB6612FNG
  VCC1 = Battery

nets:
  N1: Компонент1.A0, HC-SR04_Sensor_1.TRIG, HC-SR04_Sensor_2.TRIG, HC-SR04_Sensor_3.TRIG
  N2: Компонент1.A1, HC-SR04_Sensor_3.ECHO
  N3: Компонент1.A2, HC-SR04_Sensor_1.ECHO
  N4: Компонент1.A3, HC-SR04_Sensor_2.ECHO
  N5: Компонент1.A4/SDA, MPU6050.SDA
  N6: Компонент1.A5/SCL, MPU6050.SCL
  N7: Компонент1.D8, TB6612FNG.AIN2
  N8: Компонент1.D9_PWM, J2.pulse
  N9: Компонент1.D10_PWM/SS, Компонент2.B1
  N10: Компонент1.D11_PWM/MOSI, Компонент2.B2
  N11: Компонент1.D12/MISO, TB6612FNG.BIN1
  N12: Компонент1.D13/SCK, TB6612FNG.BIN2
  GND: Компонент1.GND, Mod1.GND, HC-SR04_Sensor_1.GND, HC-SR04_Sensor_2.GND, HC-SR04_Sensor_3.GND, MPU6050.GND, J1.pin_4, J2.gnd, J3.pin1, C1.-, C3.-, TB6612FNG.GND, VCC1.-
  N13: Компонент1.D3_PWM, J3.pin2
  N14: Компонент1.D4, TB6612FNG.STBY
  N15: Компонент1.D5_PWM, TB6612FNG.PWMA
  N16: Компонент1.D6_PWM, TB6612FNG.PWMB
  N17: Компонент1.D7, TB6612FNG.AIN1
  VCC: Компонент1.5V, Mod1.VCC, HC-SR04_Sensor_1.VCC, HC-SR04_Sensor_2.VCC, HC-SR04_Sensor_3.VCC, MPU6050.VCC, J1.pin_3, J2.vcc, C3.+, TB6612FNG.VCC
  N18: Mod1.VOT, Компонент2.A1
  N19: Mod1.VOR, Компонент2.A2
  N20: J1.pin_1, S1.leg1, C1.+, TB6612FNG.VM
  N21: S1.leg0, VCC1.+
  N22: M1.pin_1, TB6612FNG.A02
  N23: M1.pin_2, TB6612FNG.B01
  N24: M2.pin_1, TB6612FNG.A01
  N25: M2.pin_2, TB6612FNG.B02

custom parts:
  ESP32 - CAM: The ESP32-CAM has a very competitive small-size camera module that can operate independently as a minimum system with a footprint of only 27*40.5*4.5mm and a deep sleep current of up to 6mA.
  XL4015 DC-DC CC CV module (blue): XL4015 DC-DC CC/CV module blue
  TXB0108 8-channel Bi-directional Logic Level Converter: Because the Arduino (and Basic Stamp) are 5V devices, and most modern sensors, displays, flash cards and modes are 3.3V-only, many makers find that they need to perform level shifting/conversion to protect the 3.3V device from 5V. Although one can use resistors to make a divider, for high speed transfers, the resistors can add a lot of slew and cause havoc that is tough to debug. For that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
  Battery: Your standard 3x 18650 battery pack (11.1 Volts)
